// Logisim project MATIPS-BCL.circ as structural Verilog: 5 circuits, main circuit main
module main (
);

  wire and_1_out, C2, Kl2, not_1_out, or_1_out, uc2_1_aluscr, uc2_1_branch, uc2_1_datasrc, uc2_1_jump,
       uc2_1_memread_reg, uc2_1_memwrite, uc2_1_regwrite, ULA_igual;
  wire [1:0] uc2_1_aluop_2;
  wire [15:0] adder_1_out, bit_extender_1_out, bit_extender_4_out, PC_q, rom_1_data;
  wire [31:0] adder_2_out, BANCO_DE_REGISTRADORES_saida_1, BANCO_DE_REGISTRADORES_saida_2,
       bit_extender_2_out, imediato, multiplexer_1_out, multiplexer_2_out, multiplexer_3_out,
       multiplexer_4_out, multiplexer_5_out, ram_1_data, \ULA_saída ;

  Bit_Extender #(.in_width(32), .\type ("zero")) bit_extender_1 (.in(multiplexer_4_out), .out(bit_extender_1_out));
  Clock clock_1 (.out(C2));
  Register #(.width(16), .Select("low")) PC (.D(bit_extender_1_out), .Q(PC_q), .clk(C2), .clr(Kl2));  // open: en
  Button button_1 (.out(Kl2));
  Adder #(.width(16)) adder_1 (.a(16'h1), .b(PC_q), .out(adder_1_out));  // open: cin, cout
  assign bit_extender_2_out = {{16{adder_1_out[15]}}, adder_1_out};  // Bit_Extender bit_extender_2
  ROM #(.addrWidth(16), .dataWidth(16), .Select("low")) rom_1 (.addr(PC_q), .data(rom_1_data));
  UC2 uc2_1 (
    .a(rom_1_data[15]), .b(rom_1_data[14]), .c(rom_1_data[13]), .d(rom_1_data[12]), .Jump(uc2_1_jump),
    .Branch(uc2_1_branch), .MemRead_REG(uc2_1_memread_reg), .MemWrite(uc2_1_memwrite),
    .ALUOp1(uc2_1_aluop_2[1]), .ALUOp_2(uc2_1_aluop_2[0]), .ALUscr(uc2_1_aluscr), .RegWrite(uc2_1_regwrite),
    .DATASrc(uc2_1_datasrc));
  Multiplexer #(.width(32), .enable("false")) multiplexer_1 (
    .in0(multiplexer_5_out), .in1(imediato), .out(multiplexer_1_out), .sel(uc2_1_datasrc));
  assign imediato = {{28{rom_1_data[7]}}, rom_1_data[7:4]};  // Bit_Extender bit_extender_3
  BANCO_DE_REGISTRADORES BANCO_DE_REGISTRADORES (
    .WRITEDATA(multiplexer_1_out), .WRITEREG(rom_1_data[3:0]), .SAIDA_1(BANCO_DE_REGISTRADORES_saida_1),
    .R0(rom_1_data[11:8]), .SAIDA_2(BANCO_DE_REGISTRADORES_saida_2), .R1(rom_1_data[7:4]),
    .in_7(uc2_1_regwrite), .in_3(Kl2), .CLK(C2));
  or or_1 (or_1_out, uc2_1_memread_reg, uc2_1_memwrite);
  Multiplexer #(.width(32), .enable("false")) multiplexer_2 (
    .in0(BANCO_DE_REGISTRADORES_saida_2), .in1(imediato), .out(multiplexer_2_out), .sel(uc2_1_aluscr));
  Adder #(.width(32)) adder_2 (.a(bit_extender_2_out), .b(imediato), .out(adder_2_out));  // open: cin, cout
  ULA ULA (
    .ENTRADA_1(BANCO_DE_REGISTRADORES_saida_1), .ENTRADA_2(multiplexer_2_out), .\SAÍDA (\ULA_saída ),
    .IGUAL(ULA_igual), .SELETOR(uc2_1_aluop_2));
  Bit_Extender #(.in_width(32), .\type ("zero")) bit_extender_4 (.in(\ULA_saída ), .out(bit_extender_4_out));
  and and_1 (and_1_out, ULA_igual, uc2_1_branch);
  Multiplexer #(.width(32), .enable("false")) multiplexer_3 (
    .in0(bit_extender_2_out), .in1(adder_2_out), .out(multiplexer_3_out), .sel(and_1_out));
  not not_1 (not_1_out, C2);
  Multiplexer #(.width(32), .enable("false")) multiplexer_4 (
    .in0(multiplexer_3_out), .in1(adder_2_out), .out(multiplexer_4_out), .sel(uc2_1_jump));
  RAM #(.addrWidth(16), .dataWidth(32), .bus("separate"), .Select("high")) ram_1 (
    .addr(bit_extender_4_out), .din(BANCO_DE_REGISTRADORES_saida_1), .data(ram_1_data), .sel(or_1_out),
    .clk(not_1_out));  // open: str, ld, clr
  Multiplexer #(.width(32), .enable("false")) multiplexer_5 (
    .in0(\ULA_saída ), .in1(ram_1_data), .out(multiplexer_5_out), .sel(uc2_1_memread_reg));

  // Notes on the sheet:
  //   opcode
  //   contents of rom_1 (hex, n*v repeats v):
  //   0 5022 1234
  //   1010
  //   0010
  //   RS
  //   RT / IMEDIATO
  //   RD
  //   _______
  //   M A T I P S - BCL
  //   Microprocessor with Absurd Tricks without Interlocked Pipelines Stages by computer legends.
  //   __
  //   0110
  //   0100
  //   by legend ARTHUR REVERSE (WHITE BOY)
endmodule

module ULA (
  input  [31:0] ENTRADA_1,
  input  [1:0] SELETOR,
  input  [31:0] ENTRADA_2,
  output [31:0] \SAÍDA ,
  output IGUAL
);

  wire [31:0] adder_1_out, bit_extender_1_out, multiplier_1_out, subtractor_1_out;

  Adder #(.width(32)) adder_1 (.a(ENTRADA_1), .b(ENTRADA_2), .out(adder_1_out));  // open: cin, cout
  Subtractor #(.width(32)) subtractor_1 (.a(ENTRADA_1), .b(ENTRADA_2), .out(subtractor_1_out));  // open: bin, bout
  Multiplier #(.width(32)) multiplier_1 (.a(ENTRADA_1), .b(ENTRADA_2), .out(multiplier_1_out));  // open: cin, cout
  Comparator #(.width(32)) comparator_1 (.a(ENTRADA_1), .b(ENTRADA_2), .eq(IGUAL));  // open: gt, lt
  assign bit_extender_1_out = {{31{1'b0}}, IGUAL};  // Bit_Extender bit_extender_1
  Multiplexer #(.select(2), .width(32), .enable("false")) multiplexer_1 (
    .in0(adder_1_out), .in1(subtractor_1_out), .in2(bit_extender_1_out), .in3(multiplier_1_out),
    .out(\SAÍDA ), .sel(SELETOR));
endmodule

module BANCO_DE_REGISTRADORES (
  input  CLK,
  input  [3:0] R0,
  input  in_3,
  input  [31:0] WRITEDATA,
  input  [3:0] R1,
  input  [3:0] WRITEREG,
  input  in_7,
  output [31:0] SAIDA_1,
  output [31:0] SAIDA_2
);

  wire C, demultiplexer_1_out0, demultiplexer_1_out1, demultiplexer_1_out2, demultiplexer_1_out3,
       demultiplexer_1_out4, demultiplexer_1_out5, demultiplexer_1_out6, demultiplexer_1_out7,
       demultiplexer_1_out8, demultiplexer_1_out9, demultiplexer_1_out10, demultiplexer_1_out11,
       demultiplexer_1_out12, demultiplexer_1_out13, demultiplexer_1_out14, demultiplexer_1_out15;
  wire [31:0] register_1_q, register_2_q, register_3_q, register_4_q, register_5_q, register_6_q,
       register_7_q, register_8_q, register_10_q, register_11_q, register_12_q, register_13_q, register_14_q,
       register_15_q, register_16_q;

  not not_1 (C, CLK);
  Register #(.width(32), .Select("low")) register_1 (
    .D(WRITEDATA), .en(demultiplexer_1_out0), .Q(register_1_q), .clk(C), .clr(in_3));
  Register #(.width(32), .Select("low")) register_2 (
    .D(WRITEDATA), .en(demultiplexer_1_out1), .Q(register_2_q), .clk(C), .clr(in_3));
  Register #(.width(32), .Select("low")) register_3 (
    .D(WRITEDATA), .en(demultiplexer_1_out2), .Q(register_3_q), .clk(C), .clr(in_3));
  Register #(.width(32), .Select("low")) register_4 (
    .D(WRITEDATA), .en(demultiplexer_1_out3), .Q(register_4_q), .clk(C), .clr(in_3));
  Register #(.width(32), .Select("low")) register_5 (
    .D(WRITEDATA), .en(demultiplexer_1_out4), .Q(register_5_q), .clk(C), .clr(in_3));
  Register #(.width(32), .Select("low")) register_6 (
    .D(WRITEDATA), .en(demultiplexer_1_out5), .Q(register_6_q), .clk(C), .clr(in_3));
  Register #(.width(32), .Select("low")) register_7 (
    .D(WRITEDATA), .en(demultiplexer_1_out6), .Q(register_7_q), .clk(C), .clr(in_3));
  Register #(.width(32), .Select("low")) register_8 (
    .D(WRITEDATA), .en(demultiplexer_1_out7), .Q(register_8_q), .clk(C), .clr(in_3));
  Demultiplexer #(.select(4), .enable("false")) demultiplexer_1 (
    .out0(demultiplexer_1_out0), .out1(demultiplexer_1_out1), .out2(demultiplexer_1_out2),
    .out3(demultiplexer_1_out3), .out4(demultiplexer_1_out4), .out5(demultiplexer_1_out5),
    .out6(demultiplexer_1_out6), .out7(demultiplexer_1_out7), .out8(demultiplexer_1_out8),
    .out9(demultiplexer_1_out9), .out10(demultiplexer_1_out10), .out11(demultiplexer_1_out11),
    .out12(demultiplexer_1_out12), .out13(demultiplexer_1_out13), .out14(demultiplexer_1_out14),
    .out15(demultiplexer_1_out15), .in(in_7), .sel(WRITEREG));
  Register #(.width(32), .Select("low")) register_9 (
    .D(WRITEDATA), .en(demultiplexer_1_out8), .Q(register_8_q), .clk(C), .clr(in_3));
  Register #(.width(32), .Select("low")) register_10 (
    .D(WRITEDATA), .en(demultiplexer_1_out9), .Q(register_10_q), .clk(C), .clr(in_3));
  Register #(.width(32), .Select("low")) register_11 (
    .D(WRITEDATA), .en(demultiplexer_1_out10), .Q(register_11_q), .clk(C), .clr(in_3));
  Register #(.width(32), .Select("low")) register_12 (
    .D(WRITEDATA), .en(demultiplexer_1_out11), .Q(register_12_q), .clk(C), .clr(in_3));
  Register #(.width(32), .Select("low")) register_13 (
    .D(WRITEDATA), .en(demultiplexer_1_out12), .Q(register_13_q), .clk(C), .clr(in_3));
  Register #(.width(32), .Select("low")) register_14 (
    .D(WRITEDATA), .en(demultiplexer_1_out13), .Q(register_14_q), .clk(C), .clr(in_3));
  Register #(.width(32), .Select("low")) register_15 (
    .D(WRITEDATA), .en(demultiplexer_1_out14), .Q(register_15_q), .clk(C), .clr(in_3));
  Register #(.width(32), .Select("low")) register_16 (
    .D(WRITEDATA), .en(demultiplexer_1_out15), .Q(register_16_q), .clk(C), .clr(in_3));
  Multiplexer #(.select(4), .width(32), .enable("false")) multiplexer_1 (
    .in0(register_1_q), .in1(register_2_q), .in2(register_3_q), .in3(register_4_q), .in4(register_5_q),
    .in5(register_6_q), .in6(register_7_q), .in7(register_8_q), .in8(register_8_q), .in9(register_10_q),
    .in10(register_11_q), .in11(register_12_q), .in12(register_13_q), .in13(register_14_q),
    .in14(register_15_q), .in15(register_16_q), .out(SAIDA_1), .sel(R0));
  Multiplexer #(.select(4), .width(32), .enable("false")) multiplexer_2 (
    .in0(register_1_q), .in1(register_2_q), .in2(register_3_q), .in3(register_4_q), .in4(register_5_q),
    .in5(register_6_q), .in6(register_7_q), .in7(register_8_q), .in8(register_8_q), .in9(register_10_q),
    .in10(register_11_q), .in11(register_12_q), .in12(register_13_q), .in13(register_14_q),
    .in14(register_15_q), .in15(register_16_q), .out(SAIDA_2), .sel(R1));

  // Other names for the same wires on the sheet: KL = in_3
endmodule

module UC (
  input  a,
  input  b,
  input  c,
  input  d,
  output Jump,
  output Branch,
  output MemRead_REG,
  output MemWrite,
  output ALUOp1,
  output ALUOp_2,
  output ALUscr,
  output RegWrite,
  output DATASrc
);

  wire and_7_out, and_8_out, and_9_out, and_10_out, and_11_out, and_12_out, and_13_out, not_1_out, not_2_out,
       not_3_out, not_4_out, not_5_out, not_6_out, not_7_out, not_8_out, not_9_out, not_10_out, not_11_out,
       not_12_out;

  and and_1 (Jump, a, d);
  and and_2 (Branch, a, not_1_out);
  not not_1 (not_1_out, d);
  and and_3 (MemRead_REG, b, not_2_out, not_3_out);
  not not_2 (not_2_out, c);
  not not_3 (not_3_out, d);
  and and_4 (MemWrite, b, d);
  and and_5 (ALUOp1, b, c, not_4_out);
  not not_4 (not_4_out, d);
  and and_6 (ALUOp_2, c, not_5_out);
  not not_5 (not_5_out, d);
  and and_7 (and_7_out, c, d);
  and and_8 (and_8_out, b, not_6_out);
  not not_6 (not_6_out, c);
  and and_9 (and_9_out, a, d);
  not not_7 (not_7_out, a);
  and and_10 (and_10_out, not_7_out, not_8_out, d);
  not not_8 (not_8_out, b);
  not not_9 (not_9_out, b);
  and and_11 (and_11_out, not_9_out, c);
  and and_12 (and_12_out, b, not_10_out);
  not not_10 (not_10_out, c);
  and and_13 (and_13_out, b, not_11_out);
  not not_11 (not_11_out, d);
  not not_12 (not_12_out, c);
  and and_14 (DATASrc, b, not_12_out, d);
  or or_1 (ALUscr, and_7_out, and_8_out, and_9_out);
  or or_2 (RegWrite, and_10_out, and_11_out, and_12_out, and_13_out);
endmodule

module UC2 (
  input  a,
  input  b,
  input  c,
  input  d,
  output Jump,
  output Branch,
  output MemRead_REG,
  output MemWrite,
  output ALUOp1,
  output ALUOp_2,
  output ALUscr,
  output RegWrite,
  output DATASrc
);

  wire and_7_out, and_8_out, and_9_out, and_10_out, and_11_out, and_12_out, and_13_out, not_1_out, not_2_out,
       not_3_out, not_4_out, not_5_out, not_6_out, not_7_out, not_8_out, not_9_out, not_10_out, not_11_out,
       not_12_out;

  and and_1 (Jump, a, d);
  and and_2 (Branch, a, not_1_out);
  not not_1 (not_1_out, d);
  not not_2 (not_2_out, c);
  and and_3 (MemRead_REG, b, not_2_out, not_3_out);
  not not_3 (not_3_out, d);
  and and_4 (MemWrite, b, c, d);
  and and_5 (ALUOp1, b, c, not_4_out);
  not not_4 (not_4_out, d);
  and and_6 (ALUOp_2, c, not_5_out);
  not not_5 (not_5_out, d);
  and and_7 (and_7_out, c, d);
  and and_8 (and_8_out, b, not_6_out);
  not not_6 (not_6_out, c);
  and and_9 (and_9_out, a, d);
  not not_7 (not_7_out, a);
  not not_8 (not_8_out, b);
  and and_10 (and_10_out, not_7_out, not_8_out, d);
  not not_9 (not_9_out, b);
  and and_11 (and_11_out, not_9_out, c);
  and and_12 (and_12_out, b, not_10_out);
  not not_10 (not_10_out, c);
  and and_13 (and_13_out, b, not_11_out);
  not not_11 (not_11_out, d);
  and and_14 (DATASrc, b, not_12_out, d);
  not not_12 (not_12_out, c);
  or or_1 (ALUscr, and_7_out, and_8_out, and_9_out);
  or or_2 (RegWrite, and_10_out, and_11_out, and_12_out, and_13_out);
endmodule
